# Fritzing sketch rpi_datalogger (saved by Fritzing 0.9.3b)
breadboards: 1

parts:
  Raspberry_Pi1 = Raspberry Pi B+
  LED1 = smd LED [color="Red (633nm)" package="0603 [SMD]"]
  R1 = Resistor [tolerance=±5% resistance=220 package="0805 [SMD]"]
  J1 = Piezo Speaker
  Part1 = Adafruit LSM9DS1 9DoF Breakout [part_number="Adafruit #3387"]
  DS1 = DS18B20 1-Wire Temperature Sensor [part_number=DS18B20]
  R2 = Resistor [tolerance=±5% resistance=4.7k package="0402 [SMD]"]
  Part2 = Barometric Pressure Sensor - BMP180 Breakout (GY-68)

nets:
  3V3: Raspberry_Pi1.3v3, Part1.VIN, DS1.VDD, R2.Pin_1, Part2.VCC
  N1: Raspberry_Pi1.GPIO2, Part1.SDA, Part2.SDA
  N2: Raspberry_Pi1.GPIO3, Part1.SCL, Part2.SCL
  N3: Raspberry_Pi1.GPIO4, DS1.DQ, R2.Pin_0
  N4: Raspberry_Pi1.GPIO17, LED1.anode
  GND: Raspberry_Pi1.GND, R1.Pin_0, J1.pin1, Part1.GND, DS1.GND, Part2.GND
  N5: LED1.cathode, R1.Pin_1

custom parts:
  Adafruit LSM9DS1 9DoF Breakout: Add motion, direction and orientation sensing to your Arduino project with this all-in-one 9-DOF sensor. Inside the chip are three sensors, one is a classic 3-axis accelerometer, which can tell you which direction is down towards the Earth (by measuring gravity) or how fast the board is accelerating in 3D space. The other is a 3-axis magnetometer that can sense where the strongest magnetic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
